# Fritzing sketch Skech recente di mohamed (saved by Fritzing 0.9.3b)
breadboards: 1

parts:
  microSD1 = MicroSD Card Module
  Componente1 = Arduino Uno (Rev3)
  RHT1 = Humidity and Temperature Sensor RHT03
  R1 = Resistor [tolerance=±5% resistance=220 package="0603 [SMD]"]

nets:
  GND: microSD1.GND, Componente1.GND, RHT1.GND_2
  VCC: microSD1.VCC, Componente1.5V, RHT1.Vcc, R1.Pin_0
  N1: microSD1.MISO, Componente1.D12/MISO
  N2: microSD1.MOSI, Componente1.D11_PWM/MOSI
  N3: microSD1.SCK, Componente1.D13/SCK
  N4: microSD1.CS, Componente1.D10_PWM/SS
  N5: Componente1.D2, RHT1.Data-signal, R1.Pin_1
